# Fritzing sketch pot_breadboard (saved by Fritzing 0.9.4)
breadboards: 1

parts:
  Part1 = Arduino Uno (Rev3) - ICSP
  U1 = POT [package=pot_alpha_rv16af-20]
  R1 = Resistor [tolerance=±5% resistance=220 package="2512 [SMD]"]
  LED1 = LED - 3mm [color="Red (633nm)" package="3 mm [THT]"]

nets:
  N1: Part1.A0, Part1.GND, U1.A, LED1.cathode
  N2: Part1.5V, R1.Pin_1
  N3: U1.S, LED1.anode
  N4: U1.E, R1.Pin_0
