# Fritzing sketch pot_breadboard (saved by Fritzing 0.9.4)
breadboards: 1

parts:
  Part1 = Arduino Uno (Rev3) - ICSP
  10_K_Pot = POT [package=pot_alpha_rv16af-20]
  R1 = Resistor [tolerance=±5% resistance=220 package="2512 [SMD]"]
  LED1 = LED - 3mm [color="Red (633nm)" package="3 mm [THT]"]

nets:
  N1: Part1.A0, Part1.GND, 10_K_Pot.A, LED1.cathode
  N2: Part1.5V, R1.Pin_1
  N3: 10_K_Pot.S, LED1.anode
  N4: 10_K_Pot.E, R1.Pin_0
