# Fritzing sketch rgb_breadboard_setup (saved by Fritzing 0.9.4)
breadboards: 1

parts:
  Part1 = Arduino Uno (Rev3) - ICSP
  R1 = Resistor [tolerance=±5% resistance=220 package="2010 [SMD]"]
  R2 = Resistor [tolerance=±5% resistance=220 package="2010 [SMD]"]
  R3 = Resistor [tolerance=±5% resistance=220 package="2010 [SMD]"]
  LED1 = RGB LED (com. cathode, rgb) [package="5 mm [THT]"]

nets:
  N1: Part1.ICSP_MOSI, Part1.D11_PWM/MOSI, R3.Pin_1
  N2: Part1.D9_PWM, R1.Pin_1
  N3: Part1.D10_PWM/SS, R2.Pin_1
  N4: Part1.GND, LED1.common_cathode
  N5: R1.Pin_0, LED1.blue_anode
  N6: R2.Pin_0, LED1.green_anode
  N7: R3.Pin_0, LED1.red_anode
